// Logisim project ALU.circ as structural Verilog: 9 circuits, main circuit ALU
// and_array
module and_core_array (
  input  A7,
  input  A6,
  input  A5,
  input  A4,
  input  A3,
  input  A2,
  input  A1,
  input  A0,
  input  B7,
  input  B6,
  input  B5,
  input  B4,
  input  B3,
  input  B2,
  input  B1,
  input  B0,
  output S7,
  output S6,
  output S5,
  output S4,
  output S3,
  output S2,
  output S1,
  output S0
);

  and and_1 (S7, A7, B7);
  and and_2 (S6, A6, B6);
  and and_3 (S5, A5, B5);
  and and_4 (S4, A4, B4);
  and and_5 (S3, A3, B3);
  and and_6 (S2, A2, B2);
  and and_7 (S1, A1, B1);
  and and_8 (S0, A0, B0);
endmodule

// add_sub_array
module add_sub_core_array (
  input  A7,
  input  A6,
  input  A5,
  input  A4,
  input  A3,
  input  A2,
  input  A1,
  input  A0,
  input  B7,
  input  B6,
  input  B5,
  input  B4,
  input  B3,
  input  B2,
  input  B1,
  input  B0,
  input  Sub,
  output c7,
  output S7,
  output C6,
  output S6,
  output C5,
  output S5,
  output C4,
  output S4,
  output C3,
  output S3,
  output C2,
  output S2,
  output C1,
  output S1,
  output C0,
  output S0,
  output Cout
);

  wire and_1_out, and_2_out, and_3_out, and_4_out, and_5_out, and_6_out, and_7_out, and_8_out, and_9_out,
       and_10_out, and_11_out, and_12_out, and_13_out, and_14_out, and_15_out, and_16_out, xor_1_out,
       xor_2_out, xor_3_out, xor_4_out, xor_5_out, xor_6_out, xor_7_out, xor_8_out, xor_9_out, xor_10_out,
       xor_11_out, xor_12_out, xor_13_out, xor_14_out, xor_15_out, xor_16_out;

  xor xor_1 (xor_1_out, B7, Sub);
  xor xor_2 (xor_2_out, B6, Sub);
  xor xor_3 (xor_3_out, B5, Sub);
  xor xor_4 (xor_4_out, B4, Sub);
  xor xor_5 (xor_5_out, B3, Sub);
  xor xor_6 (xor_6_out, B2, Sub);
  xor xor_7 (xor_7_out, B1, Sub);
  xor xor_8 (xor_8_out, B0, Sub);
  and and_1 (and_1_out, xor_1_out, A7);
  and and_2 (and_2_out, xor_2_out, A6);
  and and_3 (and_3_out, xor_3_out, A5);
  and and_4 (and_4_out, xor_4_out, A4);
  and and_5 (and_5_out, xor_5_out, A3);
  and and_6 (and_6_out, xor_6_out, A2);
  and and_7 (and_7_out, xor_7_out, A1);
  and and_8 (and_8_out, xor_8_out, A0);
  xor xor_9 (xor_9_out, xor_1_out, A7);
  xor xor_10 (xor_10_out, xor_2_out, A6);
  xor xor_11 (xor_11_out, xor_3_out, A5);
  xor xor_12 (xor_12_out, xor_4_out, A4);
  xor xor_13 (xor_13_out, xor_5_out, A3);
  xor xor_14 (xor_14_out, xor_6_out, A2);
  xor xor_15 (xor_15_out, xor_7_out, A1);
  xor xor_16 (xor_16_out, xor_8_out, A0);
  and and_9 (and_9_out, C6, xor_9_out);
  xor xor_17 (S7, xor_9_out, C6);
  and and_10 (and_10_out, C5, xor_10_out);
  xor xor_18 (S6, xor_10_out, C5);
  and and_11 (and_11_out, C4, xor_11_out);
  xor xor_19 (S5, xor_11_out, C4);
  and and_12 (and_12_out, C3, xor_12_out);
  xor xor_20 (S4, xor_12_out, C3);
  and and_13 (and_13_out, C2, xor_13_out);
  xor xor_21 (S3, xor_13_out, C2);
  and and_14 (and_14_out, C1, xor_14_out);
  xor xor_22 (S2, xor_14_out, C1);
  and and_15 (and_15_out, C0, xor_15_out);
  xor xor_23 (S1, xor_15_out, C0);
  and and_16 (and_16_out, Sub, xor_16_out);
  xor xor_24 (S0, xor_16_out, Sub);
  or or_1 (c7, and_1_out, and_9_out);
  or or_2 (C6, and_2_out, and_10_out);
  or or_3 (C5, and_3_out, and_11_out);
  or or_4 (C4, and_4_out, and_12_out);
  or or_5 (C3, and_5_out, and_13_out);
  or or_6 (C2, and_6_out, and_14_out);
  or or_7 (C1, and_7_out, and_15_out);
  or or_8 (C0, and_8_out, and_16_out);

  assign Cout = Sub;
endmodule

module ALU (
  input  [7:0] InputA,
  input  [2:0] Op,
  input  [7:0] InputB,
  output [7:0] Sum,
  output ZeroFlag,
  output SignFlag,
  output OverflowFlag,
  output CarryFlag
);

  wire core_array_1_add_sub_cout;
  wire [7:0] core_array_1_add_sub_c, core_array_1_add_sub_s, core_array_1_and_s, core_array_1_cor_s,
       core_array_1_not_s, core_array_1_or_s;

  core_array core_array_1 (
    .A7(InputA[7]), .A6(InputA[6]), .A5(InputA[5]), .A4(InputA[4]), .A3(InputA[3]), .A2(InputA[2]),
    .A1(InputA[1]), .A0(InputA[0]), .Sub(Op[0]), .B7(InputB[7]), .B6(InputB[6]), .B5(InputB[5]),
    .B4(InputB[4]), .B3(InputB[3]), .B2(InputB[2]), .B1(InputB[1]), .B0(InputB[0]),
    .add_sub_S(core_array_1_add_sub_s), .add_sub_C(core_array_1_add_sub_c),
    .add_sub_cout(core_array_1_add_sub_cout), .and_S(core_array_1_and_s), .or_S(core_array_1_or_s),
    .not_S(core_array_1_not_s), .cor_S(core_array_1_cor_s));
  mux mux_1 (
    .op_000(core_array_1_add_sub_s), .op_001(core_array_1_add_sub_s), .op_010(core_array_1_and_s),
    .op_011(core_array_1_or_s), .op_100(core_array_1_not_s), .op_101(core_array_1_cor_s), .op(Op), .out_8(Sum));
  flag flag_1 (
    .S(Sum), .C(core_array_1_add_sub_c), .Cout(core_array_1_add_sub_cout), .ZeroFlag(ZeroFlag),
    .SignFlag(SignFlag), .OverflowFlag(OverflowFlag), .CarryFlag(CarryFlag));
endmodule

// core
module core_array (
  input  A7,
  input  A6,
  input  A5,
  input  A4,
  input  A3,
  input  A2,
  input  A1,
  input  A0,
  input  Sub,
  input  B7,
  input  B6,
  input  B5,
  input  B4,
  input  B3,
  input  B2,
  input  B1,
  input  B0,
  output [7:0] add_sub_S,
  output [7:0] add_sub_C,
  output add_sub_cout,
  output [7:0] and_S,
  output [7:0] or_S,
  output [7:0] not_S,
  output [7:0] cor_S
);

  add_sub_core_array add_sub_core_array_1 (
    .A7(A7), .A6(A6), .A5(A5), .A4(A4), .A3(A3), .A2(A2), .A1(A1), .A0(A0), .B7(B7), .B6(B6), .B5(B5),
    .B4(B4), .B3(B3), .B2(B2), .B1(B1), .B0(B0), .Sub(Sub), .c7(add_sub_C[7]), .S7(add_sub_S[7]),
    .C6(add_sub_C[6]), .S6(add_sub_S[6]), .C5(add_sub_C[5]), .S5(add_sub_S[5]), .C4(add_sub_C[4]),
    .S4(add_sub_S[4]), .C3(add_sub_C[3]), .S3(add_sub_S[3]), .C2(add_sub_C[2]), .S2(add_sub_S[2]),
    .C1(add_sub_C[1]), .S1(add_sub_S[1]), .C0(add_sub_C[0]), .S0(add_sub_S[0]), .Cout(add_sub_cout));
  and_core_array and_core_array_1 (
    .A7(A7), .A6(A6), .A5(A5), .A4(A4), .A3(A3), .A2(A2), .A1(A1), .A0(A0), .B7(B7), .B6(B6), .B5(B5),
    .B4(B4), .B3(B3), .B2(B2), .B1(B1), .B0(B0), .S7(and_S[7]), .S6(and_S[6]), .S5(and_S[5]), .S4(and_S[4]),
    .S3(and_S[3]), .S2(and_S[2]), .S1(and_S[1]), .S0(and_S[0]));
  or_core_array or_core_array_1 (
    .A7(A7), .A6(A6), .A5(A5), .A4(A4), .A3(A3), .A2(A2), .A1(A1), .A0(A0), .B7(B7), .B6(B6), .B5(B5),
    .B4(B4), .B3(B3), .B2(B2), .B1(B1), .B0(B0), .S7(or_S[7]), .S6(or_S[6]), .S5(or_S[5]), .S4(or_S[4]),
    .S3(or_S[3]), .S2(or_S[2]), .S1(or_S[1]), .S0(or_S[0]));
  not_core_array not_core_array_1 (
    .A7(A7), .A6(A6), .A5(A5), .A4(A4), .A3(A3), .A2(A2), .A1(A1), .A0(A0), .S7(not_S[7]), .S6(not_S[6]),
    .S5(not_S[5]), .S4(not_S[4]), .S3(not_S[3]), .S2(not_S[2]), .S1(not_S[1]), .S0(not_S[0]));
  xor_core_array xor_core_array_1 (
    .A7(A7), .A6(A6), .A5(A5), .A4(A4), .A3(A3), .A2(A2), .A1(A1), .A0(A0), .B7(B7), .B6(B6), .B5(B5),
    .B4(B4), .B3(B3), .B2(B2), .B1(B1), .B0(B0), .S7(cor_S[7]), .S6(cor_S[6]), .S5(cor_S[5]), .S4(cor_S[4]),
    .S3(cor_S[3]), .S2(cor_S[2]), .S1(cor_S[1]), .S0(cor_S[0]));
endmodule

// or_array
module or_core_array (
  input  A7,
  input  A6,
  input  A5,
  input  A4,
  input  A3,
  input  A2,
  input  A1,
  input  A0,
  input  B7,
  input  B6,
  input  B5,
  input  B4,
  input  B3,
  input  B2,
  input  B1,
  input  B0,
  output S7,
  output S6,
  output S5,
  output S4,
  output S3,
  output S2,
  output S1,
  output S0
);

  or or_1 (S7, A7, B7);
  or or_2 (S6, A6, B6);
  or or_3 (S5, A5, B5);
  or or_4 (S4, A4, B4);
  or or_5 (S3, A3, B3);
  or or_6 (S2, A2, B2);
  or or_7 (S1, A1, B1);
  or or_8 (S0, A0, B0);
endmodule

// not_array
module not_core_array (
  input  A7,
  input  A6,
  input  A5,
  input  A4,
  input  A3,
  input  A2,
  input  A1,
  input  A0,
  output S7,
  output S6,
  output S5,
  output S4,
  output S3,
  output S2,
  output S1,
  output S0
);

  not not_1 (S7, A7);
  not not_2 (S6, A6);
  not not_3 (S5, A5);
  not not_4 (S4, A4);
  not not_5 (S3, A3);
  not not_6 (S2, A2);
  not not_7 (S1, A1);
  not not_8 (S0, A0);
endmodule

// xor_array
module xor_core_array (
  input  A7,
  input  A6,
  input  A5,
  input  A4,
  input  A3,
  input  A2,
  input  A1,
  input  A0,
  input  B7,
  input  B6,
  input  B5,
  input  B4,
  input  B3,
  input  B2,
  input  B1,
  input  B0,
  output S7,
  output S6,
  output S5,
  output S4,
  output S3,
  output S2,
  output S1,
  output S0
);

  xor xor_1 (S7, A7, B7);
  xor xor_2 (S6, A6, B6);
  xor xor_3 (S5, A5, B5);
  xor xor_4 (S4, A4, B4);
  xor xor_5 (S3, A3, B3);
  xor xor_6 (S2, A2, B2);
  xor xor_7 (S1, A1, B1);
  xor xor_8 (S0, A0, B0);
endmodule

module mux (
  input  [7:0] op_000,
  input  [7:0] op_001,
  input  [7:0] op_010,
  input  [7:0] op_011,
  input  [7:0] op_100,
  input  [7:0] op_101,
  input  [2:0] op,
  output [7:0] out_8
);

  Multiplexer #(.select(3), .width(8)) multiplexer_1 (
    .in0(op_000), .in1(op_001), .in2(op_010), .in3(op_011), .in4(op_100), .in5(op_101), .out(out_8), .sel(op));  // open: in6, in7
endmodule

module flag (
  input  [7:0] S,
  input  [7:0] C,
  input  Cout,
  output ZeroFlag,
  output SignFlag,
  output OverflowFlag,
  output CarryFlag
);

  nor nor_1 (ZeroFlag, S[0], S[1], S[2], S[3], S[4], S[5], S[6], S[7]);
  xor xor_1 (OverflowFlag, C[6], C[7]);

  assign CarryFlag = C[7];
  assign SignFlag = S[7];
endmodule
